# Fritzing sketch power control-6 (saved by Fritzing 0.9.3b)
breadboards: 3

parts:
  C2 = Electrolytic Capacitor [capacitance=1pF package="300 mil [THT, electrolytic]"]
  IC1 = Dual Op-Amp [package=dip08]
  D2 = Zener Diode [part_number=1N4732A breakdown_voltage=3.6V package="300 mil [THT]"]
  R1 = Resistor [tolerance=±5% resistance=220 package=THT]
  R2 = Resistor [tolerance=±5% resistance=270k package=THT]
  R3 = Resistor [tolerance=±5% resistance=120k package=THT]
  D4 = SOLAR-IXYS [package=solarbit-12x1]
  R4 = Resistor [tolerance=±5% resistance=10 package=THT]
  R5 = Resistor [tolerance=±5% resistance=10 package=THT]
  DD1 = dual schottky diode TO220 [package="TO220 [THT]"]
  M1 = DC Motor
  M2 = DC Motor
  J1 = STM32 Nucleo boards
  R6 = Resistor [tolerance=±5% resistance=2.7k package=THT]
  LED2 = LEDs [package=led10mm]
  T2 = BS270 [package=to-92]
  R9 = Resistor [tolerance=±5% resistance=220 package=THT]
  U1 = Voltage Regulator - 5V [package="TO220 [THT]"]
  GPS1 = Adafruit Ultimate GPS Breakout  # not connected
  T3 = BS270 [package=to-92]
  R10 = Resistor [tolerance=±5% resistance=220 package=THT]
  R11 = Resistor [tolerance=±5% resistance=220 package=THT]
  Q1 = Basic FET N-Channel [package="TO220 [THT]"]

nets (from the schematic view):
  N1: C2.-, R5.Pin_0
  N2: C2.+, R4.Pin_0
  N3: IC1.A_OUT, Q1.gate
  N4: IC1.A_-IN, R2.Pin_1, R3.Pin_1
  VREF0: IC1.A_+IN, IC1.B_+IN, D2.cathode, R6.Pin_1
  GND: IC1.A_V-, D2.anode, R1.Pin_1, R3.Pin_0, D4.A, R5.Pin_1, M1.pin_2, M2.pin_2, T2.D, T3.D
  N5: IC1.B_-IN, R1.Pin_0, R10.Pin_1, R11.Pin_0
  N6: IC1.B_OUT, T2.G, T3.G, R11.Pin_1
  VDD: IC1.A_V+, R2.Pin_0, DD1.cathod, R6.Pin_0, R9.Pin_0, U1.input_voltage, R10.Pin_0, Q1.source
  N7: D4.C, DD1.anode_1, M1.pin_1, M2.pin_1
  N8: R4.Pin_1, Q1.drain
  N9: J1.VDD, U1.output_voltage
  N10: LED2.C, T2.S
  N11: LED2.A, R9.Pin_1
  N12: U1.GND, T3.S

custom parts:
  dual schottky diode TO220: A dual schottky diode in a TO220 package
  BS270: Generic NMOS footprint
